// Digital circuit 16XOR2.dig as structural Verilog
module _16XOR2 (
  input  [15:0] A,
  input  [15:0] B,
  output [15:0] Y
);

  xor xor_1 (Y[0], A[0], B[0]);
  xor xor_2 (Y[1], A[1], B[1]);
  xor xor_3 (Y[2], A[2], B[2]);
  xor xor_4 (Y[3], A[3], B[3]);
  xor xor_5 (Y[4], A[4], B[4]);
  xor xor_6 (Y[5], A[5], B[5]);
  xor xor_7 (Y[6], A[6], B[6]);
  xor xor_8 (Y[7], A[7], B[7]);
  xor xor_9 (Y[8], A[8], B[8]);
  xor xor_10 (Y[9], A[9], B[9]);
  xor xor_11 (Y[10], A[10], B[10]);
  xor xor_12 (Y[11], A[11], B[11]);
  xor xor_13 (Y[12], A[12], B[12]);
  xor xor_14 (Y[13], A[13], B[13]);
  xor xor_15 (Y[14], A[14], B[14]);
  xor xor_16 (Y[15], A[15], B[15]);
endmodule
