// Digital circuit CPU.dig as structural Verilog
module CPU (
  input  [7:0] Input,
  input  _1Hz,
  input  _100Hz,
  output [7:0] Output
);

  wire _74112_1_p2, _74112_1_p5, _74112_1_p8, _74112_2_p2, _74112_2_p8, _74112_3_p2, and_1_out, and_2_out,
       and_3_out, and_4_out, and_5_out, and_6_out, and_7_out, and_8_out, and_9_out, and_10_out, and_11_out,
       and_12_out, and_13_out, and_14_out, and_15_out, and_16_out, and_17_out, and_26_out, and_27_out,
       and_28_out, and_33_out, and_37_out, and_38_out, and_41_out, and_43_out, and_46_out, and_47_out,
       and_49_out, and_50_out, and_51_out, and_52_out, and_53_out, and_54_out, and_55_out, and_57_out,
       and_58_out, and_59_out, and_60_out, and_61_out, buttonled_1_p1, buttonled_1_p2, buttonled_2_p1,
       buttonled_2_p2, buttonled_3_p1, buttonled_3_p2, Clk, Clk_t, Counter_Cnt, DepthsMatch, Dir,
       director_1_dn, director_1_up, director_2_dn, director_2_up, EndOfData, fallingedge_2_q, jk_ff_1_nq,
       nand_1_out, nand_2_out, nand_3_out, nand_4_out, nand_5_out, nClk, NonZero, nor_1_out, nor_2_out,
       nor_3_out, nor_5_out, not_1_out, not_3_out, not_4_out, not_5_out, not_7_out, not_8_out, not_9_out,
       not_10_out, not_11_out, nRst, or_1_out, or_2_out, or_6_out, or_7_out, or_9_out, or_11_out, or_12_out,
       or_13_out, or_14_out, or_15_out, or_16_out, or_17_out, or_18_out, or_19_out, or_20_out, or_21_out,
       or_22_out, or_23_out, or_24_out, or_27_out, or_28_out, or_30_out, or_31_out, or_32_out, or_33_out,
       or_34_out, plus_Clk, Proceed, Pulse_out, rs_ff_as_2_q, rs_ff_as_3_q, Rst, Seek, Send_out,
       ShouldTrigger, Wiping, xor_1_out;
  wire [2:0] Step;
  wire [7:0] Changer_out, counter16_1_out, counter16_1_out_2, Data_d, not_6_out, register8_1_q,
       register8_2_q, rom_1_d, uCode_A_d, uCode_B_d;
  wire [11:4] and_18_out;
  wire [14:0] and_34_out;
  wire [15:0] _16xor2_1_y, counter16_3_out, ProgAddr;

  or or_1 (or_1_out, and_7_out, buttonled_1_p1);
  // ButtonLED buttonled_1: pin names not known; wires that end beside it: buttonled_1_p1, buttonled_1_p2
  // ButtonLED buttonled_2: pin names not known; wires that end beside it: buttonled_2_p1, buttonled_2_p2
  // ButtonLED buttonled_3: pin names not known; wires that end beside it: buttonled_3_p1, buttonled_3_p2
  nor nor_1 (nor_1_out, buttonled_2_p2, buttonled_3_p2);
  nor nor_2 (nor_2_out, buttonled_1_p2, buttonled_3_p2);
  nor nor_3 (nor_3_out, buttonled_1_p2, buttonled_2_p2);
  and and_1 (and_1_out, Clk_t, Proceed);
  FallingEdge fallingedge_1 (.I(Clk_t), .Q(Clk));
  or or_2 (or_2_out, _74112_3_p2, not_1_out);
  // _74112 _74112_1: pin names not known; wires that end beside it: and_1_out, _74112_1_p2, or_2_out, 1'b1, _74112_1_p5, _74112_1_p5, and_1_out, _74112_1_p8, _74112_1_p2, 1'b1, 1'b1, 1'b0, _74112_1_p2, _74112_1_p8
  or or_3 (buttonled_1_p2, or_1_out, nor_1_out);
  or or_4 (buttonled_2_p2, buttonled_2_p1, nor_2_out);
  or or_5 (buttonled_3_p2, buttonled_3_p1, nor_3_out);
  RisingEdge risingedge_1 (.I(Clk_t), .Q(plus_Clk));
  not not_1 (not_1_out, and_5_out);
  LED led_1 (.in(_74112_1_p2));
  and and_2 (and_2_out, buttonled_1_p2, Pulse_out);
  Button Pulse (.out(Pulse_out));
  and and_3 (and_3_out, buttonled_2_p2, _1Hz);
  and and_4 (and_4_out, buttonled_3_p2, _100Hz);
  nor nor_4 (nClk, Clk_t, Clk_t);
  or or_6 (or_6_out, and_5_out, _74112_1_p2);
  LED led_2 (.in(_74112_1_p8));
  or or_7 (or_7_out, and_2_out, and_3_out);
  or or_8 (Clk_t, or_7_out, and_4_out);
  LED led_3 (.in(Clk_t));
  and and_5 (and_5_out, _74112_1_p5, or_6_out);
  // _74112 _74112_2: pin names not known; wires that end beside it: and_1_out, _74112_2_p2, _74112_1_p8, 1'b1, _74112_1_p5, _74112_1_p5, and_1_out, _74112_2_p8, _74112_2_p2, 1'b1, 1'b1, 1'b0, _74112_2_p2, _74112_2_p8
  or or_9 (or_9_out, Rst, Counter_Cnt);
  not not_2 (Rst, nRst);
  DipSwitch #(.dipDefault("true")) nReset (.out(nRst));
  LED led_4 (.in(_74112_2_p2));
  and and_6 (and_6_out, Rst, plus_Clk);
  and and_7 (and_7_out, plus_Clk, EndOfData);
  not not_3 (not_3_out, Clk);
  LED led_5 (.in(_74112_2_p8));
  RS_FF_AS rs_ff_as_1 (.S(and_6_out), .R(and_7_out), .Q(Wiping));  // open: nQ
  not not_4 (not_4_out, or_9_out);
  and and_8 (and_8_out, plus_Clk, or_9_out);
  RS_FF_AS rs_ff_as_2 (.S(and_10_out), .R(and_8_out), .Q(rs_ff_as_2_q));  // open: nQ
  and and_9 (and_9_out, not_5_out, rs_ff_as_2_q);
  or or_10 (_74112_1_p5, and_9_out, not_3_out);
  and and_10 (and_10_out, Clk, not_4_out);
  // _74112 _74112_3: pin names not known; wires that end beside it: and_1_out, _74112_3_p2, _74112_2_p8, 1'b1, _74112_1_p5, _74112_1_p5, and_1_out, 1'b0, 1'b0, 1'b1, 1'b1, 1'b0, _74112_3_p2
  not not_5 (not_5_out, Wiping);
  Counter #(.Bits(3)) counter_1 (.en(nRst), .C(and_1_out), .clr(~_74112_1_p5), .out(Step));  // open: ovf
  LED led_6 (.in(_74112_3_p2));
  // Probe on Step
  ROM #(.AddrBits(16), .Bits(8)) rom_1 (.A(ProgAddr), .sel(1'b1), .D(rom_1_d));
  assign not_6_out = ~rom_1_d;  // Not not_6, 8 bits wide
  and and_11 (and_11_out, rom_1_d[0], rom_1_d[1], not_6_out[2], rom_1_d[3]);
  and and_12 (and_12_out, rom_1_d[0], not_6_out[1], rom_1_d[2], rom_1_d[3]);
  and and_13 (and_13_out, not_6_out[4], rom_1_d[5], not_6_out[6], not_6_out[7]);
  and and_14 (and_14_out, not_6_out[0], not_6_out[1], rom_1_d[2], rom_1_d[3]);
  and and_15 (and_15_out, not_6_out[0], rom_1_d[1], rom_1_d[2], rom_1_d[3]);
  and and_16 (and_16_out, rom_1_d[4], rom_1_d[5], not_6_out[6], not_6_out[7]);
  and and_17 (and_17_out, rom_1_d[4], not_6_out[5], rom_1_d[6], not_6_out[7]);
  and and_18 (and_18_out[4], and_11_out, and_13_out);
  and and_19 (and_18_out[5], and_12_out, and_13_out);
  and and_20 (and_18_out[6], and_14_out, and_13_out);
  and and_21 (and_18_out[7], and_15_out, and_13_out);
  and and_22 (and_18_out[8], and_14_out, and_16_out);
  and and_23 (and_18_out[9], and_15_out, and_16_out);
  and and_24 (and_18_out[10], and_11_out, and_17_out);
  and and_25 (and_18_out[11], and_12_out, and_17_out);
  or or_11 (or_11_out, or_12_out, or_13_out);
  or or_12 (or_12_out, and_18_out[5], and_18_out[4]);
  or or_13 (or_13_out, or_14_out, or_15_out);
  or or_14 (or_14_out, and_18_out[7], and_18_out[6]);
  or or_15 (or_15_out, or_16_out, or_17_out);
  or or_16 (or_16_out, and_18_out[9], and_18_out[8]);
  or or_17 (or_17_out, and_18_out[11], and_18_out[10]);
  not not_7 (not_7_out, or_11_out);
  LED led_7 (.in(and_18_out[4]));
  LED led_8 (.in(and_18_out[5]));
  LED led_9 (.in(and_18_out[6]));
  LED led_10 (.in(and_18_out[7]));
  LED led_11 (.in(and_18_out[8]));
  LED led_12 (.in(and_18_out[9]));
  LED led_13 (.in(and_18_out[10]));
  LED led_14 (.in(and_18_out[11]));
  and and_26 (and_26_out, _74112_1_p2, jk_ff_1_nq);
  ROM #(.AddrBits(12), .Bits(8)) uCode_A (.A({and_18_out, Step, Seek}), .sel(1'b1), .D(uCode_A_d));
  ROM #(.AddrBits(12), .Bits(8)) uCode_B (.A({and_18_out, Step, Seek}), .sel(1'b1), .D(uCode_B_d));
  and and_27 (and_27_out, _74112_1_p8, jk_ff_1_nq);
  or or_18 (or_18_out, and_18_out[7], and_16_out);
  and and_28 (and_28_out, _74112_2_p2, jk_ff_1_nq);
  and and_29 (and_34_out[3], _74112_2_p2, and_17_out);
  and and_30 (and_34_out[2], _74112_2_p8, and_17_out);
  and and_31 (and_34_out[1], _74112_1_p2, and_17_out);
  and and_32 (and_34_out[0], _74112_1_p8, and_17_out);
  and and_33 (and_33_out, _74112_3_p2, and_17_out);
  and and_34 (and_34_out[10], and_27_out, and_18_out[4]);
  and and_35 (and_34_out[9], and_27_out, and_18_out[5]);
  or or_19 (or_19_out, and_18_out[4], and_18_out[5]);
  or or_20 (or_20_out, or_19_out, and_18_out[7]);
  and and_36 (and_34_out[5], and_26_out, and_18_out[6]);
  and and_37 (and_37_out, and_18_out[6], and_28_out);
  and and_38 (and_38_out, and_27_out, or_18_out);
  and and_39 (and_34_out[13], and_26_out, and_18_out[8]);
  and and_40 (and_34_out[14], and_26_out, and_18_out[9]);
  and and_41 (and_41_out, _74112_2_p8, jk_ff_1_nq);
  and and_42 (and_34_out[4], and_26_out, and_18_out[7]);
  or or_21 (or_21_out, not_7_out, and_33_out);
  and and_43 (and_43_out, and_41_out, or_19_out);
  and and_44 (and_34_out[7], or_19_out, and_28_out);
  and and_45 (and_34_out[6], and_27_out, and_18_out[6]);
  and and_46 (and_46_out, and_26_out, or_20_out);
  or or_22 (or_22_out, and_37_out, and_38_out);
  and and_47 (and_47_out, and_17_out, or_27_out);
  or or_23 (or_23_out, _74112_1_p2, _74112_1_p8);
  or or_24 (or_24_out, or_21_out, and_43_out);
  and and_48 (and_34_out[8], or_19_out, and_26_out);
  or or_25 (and_34_out[12], and_34_out[7], and_34_out[6]);
  or or_26 (and_34_out[11], and_46_out, and_47_out);
  or or_27 (or_27_out, or_23_out, _74112_2_p2);
  and and_49 (and_49_out, _74112_3_p2, Seek);
  or or_28 (or_28_out, or_24_out, or_22_out);
  LED led_15 (.in(and_34_out[3]));
  LED led_16 (.in(and_34_out[2]));
  LED led_17 (.in(and_34_out[1]));
  LED led_18 (.in(and_34_out[0]));
  xor xor_1 (xor_1_out, and_18_out[11], Dir);
  _16XOR2 _16xor2_1 (.A({uCode_A_d, uCode_B_d}), .B({Counter_Cnt, and_34_out}), .Y(_16xor2_1_y));
  or or_29 (Counter_Cnt, and_49_out, or_28_out);
  and and_50 (and_50_out, NonZero, and_18_out[11]);
  not not_8 (not_8_out, NonZero);
  not not_9 (not_9_out, Seek);
  not not_10 (not_10_out, ShouldTrigger);
  and and_51 (and_51_out, not_10_out, xor_1_out);
  LED led_19 (.in(_16xor2_1_y[15]));
  LED led_20 (.in(_16xor2_1_y[14]));
  LED led_21 (.in(_16xor2_1_y[13]));
  LED led_22 (.in(_16xor2_1_y[12]));
  LED led_23 (.in(_16xor2_1_y[11]));
  LED led_24 (.in(_16xor2_1_y[10]));
  LED led_25 (.in(_16xor2_1_y[9]));
  LED led_26 (.in(_16xor2_1_y[8]));
  LED led_27 (.in(_16xor2_1_y[7]));
  LED led_28 (.in(_16xor2_1_y[6]));
  LED led_29 (.in(_16xor2_1_y[5]));
  LED led_30 (.in(_16xor2_1_y[4]));
  LED led_31 (.in(_16xor2_1_y[3]));
  LED led_32 (.in(_16xor2_1_y[2]));
  LED led_33 (.in(_16xor2_1_y[1]));
  LED led_34 (.in(_16xor2_1_y[0]));
  or or_30 (or_30_out, and_50_out, and_52_out);
  and and_52 (and_52_out, not_8_out, and_18_out[10]);
  and and_53 (and_53_out, ShouldTrigger, and_34_out[3]);
  and and_54 (and_54_out, DepthsMatch, and_34_out[2]);
  and and_55 (and_55_out, not_9_out, ShouldTrigger);
  Director director_1 (.En(and_34_out[0]), .Clk(plus_Clk), .Dir(and_51_out), .Up(director_1_up), .Dn(director_1_dn));
  and and_56 (ShouldTrigger, or_30_out, jk_ff_1_nq);
  or or_31 (or_31_out, Rst, and_54_out);
  nand nand_1 (nand_1_out, and_55_out, and_34_out[1]);
  Counter16 counter16_1 (
    .nUp(director_1_up), .nDn(director_1_dn), .In({16{1'b0}}), .nLd(1'b1), .Clr(Rst),
    .Out({counter16_1_out_2, counter16_1_out}));  // open: nBO
  LED led_35 (.in(ShouldTrigger));
  and and_57 (and_57_out, and_53_out, and_18_out[11]);
  Register8 register8_1 (.nEn(nand_1_out), .D(counter16_1_out), .Clk(Clk_t), .Q(register8_1_q));
  Register8 register8_2 (.nEn(nand_1_out), .D(counter16_1_out_2), .Clk(Clk_t), .Q(register8_2_q));
  LED led_36 (.in(Counter_Cnt));
  LED led_37 (.in(and_34_out[14]));
  LED led_38 (.in(and_34_out[13]));
  LED led_39 (.in(and_34_out[12]));
  LED led_40 (.in(and_34_out[11]));
  LED led_41 (.in(and_34_out[10]));
  LED led_42 (.in(and_34_out[9]));
  LED led_43 (.in(and_34_out[8]));
  LED led_44 (.in(and_34_out[7]));
  LED led_45 (.in(and_34_out[6]));
  LED led_46 (.in(and_34_out[5]));
  LED led_47 (.in(and_34_out[4]));
  JK_FF jk_ff_1 (.J(and_53_out), .C(~nClk), .K(or_31_out), .Q(Seek), .nQ(jk_ff_1_nq));
  JK_FF jk_ff_2 (.J(and_57_out), .C(~nClk), .K(or_31_out), .Q(Dir));  // open: nQ
  nand nand_2 (nand_2_out, plus_Clk, and_34_out[10]);
  nand nand_3 (nand_3_out, plus_Clk, and_34_out[9]);
  nand nand_4 (nand_4_out, plus_Clk, and_34_out[8]);
  and and_58 (and_58_out, Wiping, Clk_t);
  and and_59 (and_59_out, plus_Clk, and_34_out[14]);
  nand nand_5 (nand_5_out, plus_Clk, and_34_out[13]);
  and and_60 (and_60_out, Clk_t, and_34_out[5]);
  Equal equal_1 (.A({register8_2_q, register8_1_q}), .B({counter16_1_out_2, counter16_1_out}), .Eq(DepthsMatch));
  nor nor_5 (nor_5_out, and_58_out, and_59_out);
  FallingEdge fallingedge_2 (.I(Wiping), .Q(fallingedge_2_q));
  or or_32 (or_32_out, Wiping, and_34_out[12]);
  not not_11 (not_11_out, and_34_out[4]);
  LED led_48 (.in(Seek));
  LED led_49 (.in(Dir));
  // Probe on {register8_2_q, register8_1_q}
  // Probe on {counter16_1_out_2, counter16_1_out}
  or or_33 (or_33_out, Rst, fallingedge_2_q);
  or or_34 (or_34_out, Rst, Send_out);
  Director director_2 (.En(Counter_Cnt), .Clk(plus_Clk), .Dir(Dir), .Up(director_2_up), .Dn(director_2_dn));
  RAMDualPort #(.AddrBits(16), .Bits(8)) Data (
    .A(counter16_3_out), .Din(Data_d), .str(or_32_out), .C(Clk_t), .ld(and_34_out[11]), .D(Data_d));
  Counter8 Changer (
    .nUp(nand_2_out), .nDn(nand_3_out), .In(Data_d), .nLd(nand_4_out), .Clr(Rst), .Out(Changer_out));  // open: nBO
  assign Data_d = and_34_out[7] ? Changer_out : 8'bz;  // Driver driver_1
  assign Data_d = and_34_out[6] ? Input : 8'bz;  // Driver driver_2
  RS_FF_AS rs_ff_as_3 (.S(and_60_out), .R(or_34_out), .Q(rs_ff_as_3_q), .nQ(Proceed));
  Register8 register8_3 (.nEn(not_11_out), .D(Data_d), .Clk(Clk_t), .Q(Output));
  Nonzero nonzero_1 (.D(Data_d), .NZ(NonZero));
  PullDown #(.Bits(8)) pulldown_1 (.out(Data_d));
  Counter16 counter16_2 (
    .nUp(director_2_up), .nDn(director_2_dn), .In({16{1'b0}}), .nLd(1'b1), .Clr(Rst), .Out(ProgAddr));  // open: nBO
  Counter16 counter16_3 (
    .nUp(nor_5_out), .nDn(nand_5_out), .In({16{1'b0}}), .nLd(1'b1), .Clr(or_33_out), .Out(counter16_3_out));  // open: nBO
  and and_61 (and_61_out, Clk_t, and_34_out[4]);
  // Probe on counter16_3_out
  EndOfAddress endofaddress_1 (.D(counter16_3_out), .End(EndOfData));
  // Probe on Data_d
  // Probe on Changer_out
  LED led_50 (.in(rs_ff_as_3_q));
  Button Send (.out(Send_out));
  LED led_51 (.in(and_61_out));
  // Probe on ProgAddr

  // Notes on the sheet:
  //   _100Hz: Hz: 100
  //   RAM chip connections:
  //   ~WE = Data_In NAND +Clk
  //   ~OE = DATA_Out
  //   ~CS = 0
  //   Alternatively:
  //   LowerRAM.~CS = A_15
  //   UpperRAM.~CS = NOT A_15
  //   Clock Generation
  //   Wire colors:
  //   Clock lines - yellow
  //   Step lines/logic - red
  //   Decoding logic - green
  //   Decision logic - blue
  //   Manupulation logic - white
  //   rom_1 loads program.bf
  //   +
  //   -
  //   ,
  //   .
  //   <
  //   >
  //   [
  //   ]
  //   uCode_A loads ucodeA.bin
  //   uCode_B loads ucodeB.bin
  //   Counter_Cnt
  //   Pointer_Inc
  //   Pointer_Dec
  //   Data_In
  //   Data_Out
  //   Changer_Add
  //   Changer_Sub
  //   Changer_In
  //   Changer_Out
  //   Input_Out
  //   Input_Await
  //   Output_In
  //   TrySeek
  //   TryStopSeek
  //   TryLatchDepth
  //   CountDepth
  //   Depth
  //   Seek
  //   Dir
  //   Target Depth
  //   Current Depth
  //   Counter
  //   Pointer
endmodule
