// Digital circuit Counter16.dig as structural Verilog
module Counter16 (
  input  En,
  input  Clk,
  input  Dir,
  input  [15:0] In,
  input  Ld,
  input  Clr,
  output Out
);

  wire _74193_1_p1, _74193_1_p4, _74193_1_p5, _74193_1_p6, _74193_1_p11, _74193_1_p12, _74193_1_p13,
       _74193_1_p14, _74193_1_p15, _74193_1_p16, _74193_2_p7, _74193_2_p8, _74193_2_p9, _74193_2_p10,
       _74193_2_p11, _74193_2_p12, button_1_out, button_2_out, dipswitch_1_out, dipswitch_2_out;

  Button #(.activeLow("true")) button_1 (.out(button_1_out));
  Button #(.activeLow("true")) button_2 (.out(button_2_out));
  DipSwitch dipswitch_1 (.out(dipswitch_1_out));
  DipSwitch dipswitch_2 (.out(dipswitch_2_out));
  // _74193 _74193_1: pin names not known; wires that end beside it: _74193_1_p1, button_1_out, button_2_out, _74193_1_p4, _74193_1_p5, _74193_1_p6, dipswitch_1_out, dipswitch_2_out, 1'b1, 1'b0, _74193_1_p11, _74193_1_p12, _74193_1_p13, _74193_1_p14, _74193_1_p15, _74193_1_p16, _74193_1_p13, _74193_1_p14, _74193_1_p15, _74193_1_p16, Out
  // _74193 _74193_2: pin names not known; wires that end beside it: _74193_1_p11, _74193_1_p12, dipswitch_1_out, dipswitch_2_out, 1'b1, 1'b0, _74193_2_p7, _74193_2_p8, _74193_2_p9, _74193_2_p10, _74193_2_p11, _74193_2_p12, _74193_2_p7, _74193_2_p8, _74193_2_p9, _74193_2_p10, _74193_2_p11, _74193_2_p12
endmodule
