// Digital circuit Counter4.dig as structural Verilog
module Counter4 (
  input  nPL,
  input  nU_D,
  input  CP,
  input  nCE,
  input  [3:0] In,
  output [3:0] Out,
  output nRC
);

  // _74191 _74191_1: pin names not known; wires that end beside it: In[0], nPL, nU_D, CP, nCE, In[1], In[2], In[3], 1'b1, 1'b0, Out[0], Out[1], Out[2], Out[3], nRC
endmodule
