// Digital circuit Counter8.dig as structural Verilog
module Counter8 (
  input  nUp,
  input  nDn,
  input  [7:0] In,
  input  nLd,
  input  Clr,
  output [7:0] Out,
  output nBO
);

  wire _74193_1_p12, _74193_2_p11, _74193_2_p12;

  // _74193 _74193_1: pin names not known; wires that end beside it: In[0], nDn, nUp, In[1], In[2], In[3], Clr, nLd, 1'b1, 1'b0, nBO, _74193_1_p12, Out[0], Out[1], Out[2], Out[3]
  // _74193 _74193_2: pin names not known; wires that end beside it: In[4], nBO, _74193_1_p12, In[5], In[6], In[7], Clr, nLd, 1'b1, 1'b0, _74193_2_p11, _74193_2_p12, Out[4], Out[5], Out[6], Out[7], _74193_2_p11, _74193_2_p12
endmodule
