// Digital circuit Director.dig as structural Verilog
module Director (
  input  En,
  input  Clk,
  input  Dir,
  output Up,
  output Dn
);

  wire and_1_out, and_2_out, not_1_out;

  not not_1 (not_1_out, Dir);
  and and_1 (and_1_out, Clk, not_1_out);
  and and_2 (and_2_out, Clk, Dir);
  nand nand_1 (Up, and_1_out, En);
  nand nand_2 (Dn, and_2_out, En);
endmodule
