// Digital circuit Encoder.dig as structural Verilog
module Encoder (
  input  I0,
  input  I1,
  input  I2,
  input  I3,
  input  I4,
  input  I5,
  input  I6,
  input  I7,
  output Invalid,
  output O2,
  output O1,
  output O0
);

  wire or_4_out;

  or or_1 (O0, I1, I3, I5, I7);
  or or_2 (O1, I2, I3, I6, I7);
  or or_3 (O2, I4, I5, I6, I7);
  or or_4 (or_4_out, I0, O2, O1, O0);
  not not_1 (Invalid, or_4_out);

  // Notes on the sheet:
  //   NOTE: If multiple inputs are
  //   triggered, output is bitwise
  //   OR of the binary of all
  //   active inputs.
endmodule
