// Digital circuit EndOfAddress.dig as structural Verilog
module EndOfAddress (
  input  [15:0] D,
  output End
);

  wire and_1_out, and_2_out, and_3_out, and_4_out, and_6_out, and_7_out, and_8_out, and_9_out, and_10_out,
       and_11_out, and_12_out, and_13_out, and_14_out;

  and and_1 (and_1_out, D[0], D[1]);
  and and_2 (and_2_out, and_13_out, D[8]);
  and and_3 (and_3_out, and_1_out, D[2]);
  and and_4 (and_4_out, and_2_out, D[9]);
  and and_5 (End, and_3_out, D[3]);
  and and_6 (and_6_out, and_4_out, D[10]);
  and and_7 (and_7_out, End, D[4]);
  and and_8 (and_8_out, and_6_out, D[11]);
  and and_9 (and_9_out, and_7_out, D[5]);
  and and_10 (and_10_out, and_8_out, D[12]);
  and and_11 (and_11_out, and_9_out, D[6]);
  and and_12 (and_12_out, and_10_out, D[13]);
  and and_13 (and_13_out, and_11_out, D[7]);
  and and_14 (and_14_out, and_12_out, D[14]);
  // And and_15 has open pins: In_1=and_14_out, In_2=D[15], out=open

  // Notes on the sheet:
  //   To cut off RAM wiping sooner, connect the
  //   upper address bits to 1 instead of A_n or
  //   just connect the output to an AND sooner
  //   in the chain.
endmodule
