// Digital circuit Equal.dig as structural Verilog
module Equal (
  input  [15:0] A,
  input  [15:0] B,
  output Eq
);

  wire or_1_out, or_2_out, or_3_out, or_4_out, or_5_out, or_6_out, or_7_out, or_8_out, or_9_out, or_10_out,
       or_11_out, or_12_out, or_13_out, or_14_out, or_15_out, xor_1_out, xor_2_out, xor_3_out, xor_4_out,
       xor_5_out, xor_6_out, xor_7_out, xor_8_out, xor_9_out, xor_10_out, xor_11_out, xor_12_out, xor_13_out,
       xor_14_out, xor_15_out, xor_16_out;

  xor xor_1 (xor_1_out, A[0], B[0]);
  xor xor_2 (xor_2_out, A[1], B[1]);
  xor xor_3 (xor_3_out, A[2], B[2]);
  xor xor_4 (xor_4_out, A[3], B[3]);
  xor xor_5 (xor_5_out, A[4], B[4]);
  xor xor_6 (xor_6_out, A[5], B[5]);
  xor xor_7 (xor_7_out, A[6], B[6]);
  xor xor_8 (xor_8_out, A[7], B[7]);
  xor xor_9 (xor_9_out, A[8], B[8]);
  xor xor_10 (xor_10_out, A[9], B[9]);
  xor xor_11 (xor_11_out, A[10], B[10]);
  xor xor_12 (xor_12_out, A[11], B[11]);
  xor xor_13 (xor_13_out, A[12], B[12]);
  xor xor_14 (xor_14_out, A[13], B[13]);
  xor xor_15 (xor_15_out, A[14], B[14]);
  xor xor_16 (xor_16_out, A[15], B[15]);
  not not_1 (Eq, or_1_out);
  or or_1 (or_1_out, xor_1_out, or_2_out);
  or or_2 (or_2_out, xor_2_out, or_3_out);
  or or_3 (or_3_out, xor_3_out, or_4_out);
  or or_4 (or_4_out, xor_4_out, or_5_out);
  or or_5 (or_5_out, xor_5_out, or_6_out);
  or or_6 (or_6_out, xor_6_out, or_7_out);
  or or_7 (or_7_out, xor_7_out, or_8_out);
  or or_8 (or_8_out, xor_8_out, or_9_out);
  or or_9 (or_9_out, xor_9_out, or_10_out);
  or or_10 (or_10_out, xor_10_out, or_11_out);
  or or_11 (or_11_out, xor_11_out, or_12_out);
  or or_12 (or_12_out, xor_12_out, or_13_out);
  or or_13 (or_13_out, xor_13_out, or_14_out);
  or or_14 (or_14_out, xor_14_out, or_15_out);
  or or_15 (or_15_out, xor_15_out, xor_16_out);
endmodule
