// Digital circuit Nonzero.dig as structural Verilog
module Nonzero (
  input  [7:0] D,
  output NZ
);

  wire or_1_out, or_2_out, or_3_out, or_4_out, or_5_out, or_6_out;

  or or_1 (or_1_out, D[0], D[1]);
  or or_2 (or_2_out, or_1_out, D[2]);
  or or_3 (or_3_out, or_2_out, D[3]);
  or or_4 (or_4_out, or_3_out, D[4]);
  or or_5 (or_5_out, or_4_out, D[5]);
  or or_6 (or_6_out, or_5_out, D[6]);
  or or_7 (NZ, or_6_out, D[7]);
endmodule
