// Digital circuit Register16.dig as structural Verilog
module Register16 (
  input  nEn,
  input  [15:0] D,
  input  Clk,
  output [15:0] Q
);

  // _74377 _74377_1: pin names not known; wires that end beside it: D[0], 1'b1, 1'b0, D[1], D[2], D[3], nEn, D[4], D[5], D[6], D[7], Clk, Q[0], Q[1], Q[2], Q[3], Q[4], Q[5], Q[6], Q[7]
  // _74377 _74377_2: pin names not known; wires that end beside it: D[8], 1'b1, 1'b0, D[9], D[10], D[11], nEn, D[12], D[13], D[14], D[15], Clk, Q[8], Q[9], Q[10], Q[11], Q[12], Q[13], Q[14], Q[15]
endmodule
