// Digital circuit Register8.dig as structural Verilog
module Register8 (
  input  nEn,
  input  [7:0] D,
  input  Clk,
  output [7:0] Q
);

  // _74377 _74377_1: pin names not known; wires that end beside it: D[0], 1'b1, 1'b0, D[1], D[2], D[3], nEn, D[4], D[5], D[6], D[7], Clk, Q[0], Q[1], Q[2], Q[3], Q[4], Q[5], Q[6], Q[7]
endmodule
