// Digital circuit RisingEdge.dig as structural Verilog
module RisingEdge (
  input  I,
  output Q
);

  wire delay_1_out, not_1_out;

  not not_1 (not_1_out, delay_1_out);
  Delay #(.delayTime(10)) delay_1 (.in(I), .out(delay_1_out));
  and and_1 (Q, I, not_1_out);
endmodule
