// Digital circuit resetTiming.dig as structural Verilog
module resetTiming (
);

  wire and_1_out, and_2_out, and_3_out, and_4_out, and_5_out, and_6_out, and_7_out, Clk, Clk_out, Cntr_Clr,
       Data_Str, Enable, EndOfAddress, EndOfAddress_out, nClk, not_1_out, nPntr_Up, nReset_out, nRst,
       Pntr_Clr, rs_ff_as_1_q, rs_ff_as_3_nq, rs_ff_as_4_q, rs_ff_as_5_q, rs_ff_as_7_nq, rs_ff_as_7_q;

  DipSwitch u_Clk (.out(Clk_out));
  xor xor_1 (Clk, Clk_out, 1'b0);
  xor xor_2 (nClk, Clk_out, 1'b1);
  Button u_EndOfAddress (.out(EndOfAddress_out));
  and and_1 (and_1_out, EndOfAddress, Clk);
  and and_2 (and_2_out, Clk, rs_ff_as_5_q);
  and and_3 (and_3_out, Clk, EndOfAddress_out);
  RS_FF_AS rs_ff_as_1 (.S(and_1_out), .R(and_2_out), .Q(rs_ff_as_1_q));  // open: nQ
  RS_FF_AS rs_ff_as_2 (.S(and_2_out), .R(Cntr_Clr), .Q(Enable));  // open: nQ
  RS_FF_AS rs_ff_as_3 (.S(Cntr_Clr), .R(rs_ff_as_5_q), .Q(Data_Str), .nQ(rs_ff_as_3_nq));
  RS_FF_AS rs_ff_as_4 (.S(and_3_out), .R(Pntr_Clr), .Q(rs_ff_as_4_q));  // open: nQ
  and and_4 (and_4_out, nClk, rs_ff_as_1_q);
  or or_1 (nPntr_Up, rs_ff_as_3_nq, nClk);
  and and_5 (and_5_out, nClk, rs_ff_as_4_q);
  RS_FF_AS rs_ff_as_5 (.S(and_4_out), .R(and_2_out), .Q(rs_ff_as_5_q));  // open: nQ
  not not_1 (not_1_out, nReset_out);
  DipSwitch #(.dipDefault("true")) nReset (.out(nReset_out));
  and and_6 (and_6_out, nReset_out, nClk);
  RS_FF_AS rs_ff_as_6 (.S(and_5_out), .R(Pntr_Clr), .Q(EndOfAddress));  // open: nQ
  or or_2 (Pntr_Clr, Cntr_Clr, rs_ff_as_5_q);
  RS_FF_AS rs_ff_as_7 (.S(not_1_out), .R(and_6_out), .Q(rs_ff_as_7_q), .nQ(rs_ff_as_7_nq));
  and and_7 (and_7_out, rs_ff_as_7_nq, Clk);
  RS_FF_AS rs_ff_as_8 (.S(rs_ff_as_7_q), .R(and_7_out), .Q(Cntr_Clr), .nQ(nRst));
  LED led_1 (.in(Clk));
  LED led_2 (.in(Cntr_Clr));
  LED led_3 (.in(Cntr_Clr));
  LED led_4 (.in(Pntr_Clr));
  LED led_5 (.in(EndOfAddress));
  LED led_6 (.in(nPntr_Up));
  LED led_7 (.in(Data_Str));
  LED led_8 (.in(Enable));

  // Other names for the same wires on the sheet: Rst = Cntr_Clr

  // Notes on the sheet:
  //   Clock Generation
  //   Temp EndOfAddress Trigger
  //   Data Wipe Sequencing
  //   Reset Timing
  //   Signal Display
  //   EndOfAddress goes
  //   high on -Clk when
  //   the wiping process is complete
  //   EndOfAddress will be
  //   determined by the value
  //   of Cntr
endmodule
