// Digital circuit test.dig as structural Verilog
module test (
  input  _10Hz,
  input  BallsToTheWall,
  input  _2Hz
);

  wire _74112_1_p2, _74112_1_p8, _74112_2_p2, _74112_2_p8, _74112_3_p2, and_1_out, and_2_out, and_3_out, Clk,
       Clk_t, nand_1_out, nClk, not_1_out, not_4_out, nRst, nStep_Rst, or_1_out, or_2_out, plus_Clk, Proceed,
       Pulse_out, rs_ff_as_1_q, Rst, Wiping;
  wire [1:0] dipswitch_2_out;

  and and_1 (and_1_out, not_1_out, rs_ff_as_1_q);
  not not_1 (not_1_out, Wiping);
  and and_2 (and_2_out, Clk_t, Proceed);
  RS_FF_AS rs_ff_as_1 (.S(plus_Clk), .R(nand_1_out), .Q(rs_ff_as_1_q));  // open: nQ
  nand nand_1 (nand_1_out, nStep_Rst, nRst);
  DipSwitch #(.dipDefault("true")) nReset (.out(nRst));
  Button Pulse (.out(Pulse_out));
  DipSwitch dipswitch_1 (.out(dipswitch_2_out[1]));
  DipSwitch dipswitch_2 (.out(dipswitch_2_out[0]));
  not not_2 (Rst, nRst);
  Multiplexer #(.Selector_Bits(2)) multiplexer_1 (
    .sel(dipswitch_2_out), .in_0(Pulse_out), .in_1(_2Hz), .in_2(_10Hz), .in_3(BallsToTheWall), .out(Clk_t));
  or or_1 (or_1_out, _74112_3_p2, not_4_out);
  not not_3 (nClk, Clk_t);
  RisingEdge risingedge_1 (.I(Clk_t), .Q(plus_Clk));
  FallingEdge fallingedge_1 (.I(Clk_t), .Q(Clk));
  LED led_1 (.in(Clk_t));
  not not_4 (not_4_out, and_3_out);
  // _74112 _74112_1: pin names not known; wires that end beside it: and_2_out, _74112_1_p2, or_1_out, 1'b1, and_1_out, and_1_out, and_2_out, _74112_1_p8, _74112_1_p2, 1'b1, 1'b1, 1'b0, _74112_1_p2, _74112_1_p8
  or or_2 (or_2_out, _74112_1_p2, and_3_out);
  LED led_2 (.in(_74112_1_p2));
  and and_3 (and_3_out, and_1_out, or_2_out);
  LED led_3 (.in(_74112_1_p8));
  // _74112 _74112_2: pin names not known; wires that end beside it: and_2_out, _74112_2_p2, _74112_1_p8, 1'b1, and_1_out, and_1_out, and_2_out, _74112_2_p8, _74112_2_p2, 1'b1, 1'b1, 1'b0, _74112_2_p2, _74112_2_p8
  LED led_4 (.in(_74112_2_p8));
  LED led_5 (.in(_74112_2_p2));
  // _74112 _74112_3: pin names not known; wires that end beside it: and_2_out, _74112_3_p2, _74112_2_p8, 1'b1, and_1_out, and_1_out, and_2_out, 1'b0, 1'b0, 1'b1, 1'b1, 1'b0, _74112_3_p2
  LED led_6 (.in(_74112_3_p2));

  // Notes on the sheet:
  //   _10Hz: Hz: 10
  //   BallsToTheWall: Hz: 2147483647
  //   _2Hz: Hz: 2
  //   Clock Select
endmodule
